# Fritzing sketch _elektronikschema (saved by Fritzing 1.0.4)
breadboards: 1

parts:
  Part1 = Arduino Mega 2560 (Rev3)
  HC-SR04_Sensor_1 = HC-SR04 Ultrasonic Distance Sensor
  HC-SR04_Sensor_2 = HC-SR04 Ultrasonic Distance Sensor
  HC-SR04_Sensor_3 = HC-SR04 Ultrasonic Distance Sensor
  MIC1 = Microphone
  Part3 = Humidity Temperature Sensor SHT15
  Part2 = Ambient Light Sensor (TEMT6000 Breakout Board)
  Disp1 = 60mm 8x8 dot matrix row cathode led display with narrow pcb pads  # not connected
  J1 = Power Jack [package=power_jack_pth]  # not connected
  DS1 = DS18B20 1-Wire Temperature Sensor [part_number=DS18B20]  # not connected

nets:
  N1: Part1.D13_PWM, HC-SR04_Sensor_3.TRIG
  N2: Part1.D12_PWM, HC-SR04_Sensor_3.ECHO
  N3: Part1.D11_PWM, HC-SR04_Sensor_2.TRIG
  N4: Part1.D10_PWM, HC-SR04_Sensor_1.ECHO
  N5: Part1.D9_PWM, HC-SR04_Sensor_1.TRIG
  N6: Part1.D8_PWM, HC-SR04_Sensor_2.ECHO
  VCC: Part1.5V, HC-SR04_Sensor_1.VCC, HC-SR04_Sensor_2.VCC, HC-SR04_Sensor_3.VCC, MIC1.pin2, Part3.SCL, Part2.VCC
  GND: Part1.GND, HC-SR04_Sensor_1.GND, HC-SR04_Sensor_2.GND, HC-SR04_Sensor_3.GND, MIC1.pin1, Part3.GND, Part2.GND
  N7: Part1.D5_PWM, Part2.S
  N8: Part1.D6_PWM, Part3.SDA
